# Fritzing sketch Mikrocontroller_Intro (saved by Fritzing 0.9.10b)
breadboards: 1

parts:
  R1 = Resistor [tolerance=±5% power=0.25 resistance=220 package=THT]
  R2 = Resistor [tolerance=±5% power=0.25 resistance=10k package=THT]
  R3 = Photocell (LDR) [package=THT]
  LED1 = LED - 5mm [color="Red (633nm)" current=0.030 package="5 mm [THT]"]
  R4 = Rotary Potentiometer (Small) [maximum_resistance=100kΩ knob_status=50% power=0.5W package=THT]
  S1 = Momentary Switch [package=ksa_sealed_tac_switch]
  Bauteil1 = Arduino Uno (Rev3) - ICSP
  R5 = Resistor [tolerance=±5% power=0.25 resistance=10k package=THT]

nets:
  N1: R1.Pin_0, LED1.anode
  N2: R1.Pin_1, Bauteil1.D3_PWM
  N3: R2.Pin_0, LED1.cathode, R4.leg1, Bauteil1.GND, R5.Pin_0
  N4: R2.Pin_1, R3.pin_0, Bauteil1.A0
  N5: R3.pin_1, R4.leg2, S1.1, Bauteil1.5V
  N6: R4.wiper, Bauteil1.A1
  N7: S1.3, Bauteil1.D2, R5.Pin_1
